# Fritzing sketch fram-tester_breadboard (saved by Fritzing 0.9.3b)
breadboards: 1

parts:
  IC1 = IC, DIP package, 28 pins [chip_label="FRAM (Socket)"]
  Q1 = PNP-Transistor [package="TO92 [THT]"]
  U2 = 74HC595 [package="DIP16 [THT]"]
  Part1 = Arduino Nano (Rev3.0)
  U1 = 74HC595 [package="DIP16 [THT]"]

nets:
  A14: IC1.pin1, U2.Q6
  A12: IC1.pin2, U2.Q4
  A7: IC1.pin3, U1.Q7
  A6: IC1.pin4, U1.Q6
  A5: IC1.pin5, U1.Q5
  A4: IC1.pin6, U1.Q4
  A3: IC1.pin7, U1.Q3
  A2: IC1.pin8, U1.Q2
  A1: IC1.pin9, U1.Q1
  A0: IC1.pin10, U1.Q0
  D0: IC1.pin11, Part1.D0/RX
  D1: IC1.pin12, Part1.D1/TX
  D2: IC1.pin13, Part1.D2
  GND: IC1.pin14, U2.GND, U2.OE, Part1.GND, U1.GND, U1.OE
  D3: IC1.pin15, Part1.D3
  D4: IC1.pin16, Part1.D4
  D5: IC1.pin17, Part1.D5
  D6: IC1.pin18, Part1.D6
  D7: IC1.pin19, Part1.D7
  ^CE: IC1.pin20, Part1.D11/MOSI
  A10: IC1.pin21, U2.Q2
  ^OE: IC1.pin22, Part1.D12/MISO
  A11: IC1.pin23, U2.Q3
  A9: IC1.pin24, U2.Q1
  A8: IC1.pin25, U2.Q0
  A13: IC1.pin26, U2.Q5
  ^WE: IC1.pin27, Part1.D13/SCK
  N1: IC1.pin28, Q1.C
  5V: Q1.E, U2.MR, U2.VCC, Part1.5V, U1.MR, U1.VCC
  GOODNIGHT: Q1.B, Part1.A0
  SR_SHIFT: U2.SH_CP, Part1.D10, U1.SH_CP
  SR_LATCH: U2.ST_CP, Part1.D9, U1.ST_CP
  N2: U2.DS, U1.Q7'
  DS: Part1.D8, U1.DS
